// Logisim project 1_*.circ as structural Verilog: 3 circuits, main circuit main
module main (
  input  in_1,
  input  in_2,
  output out_3
);

  wire nand_1_out;

  nand nand_1 (nand_1_out, in_1, in_2);
  not nand_2 (out_3, nand_1_out);  // NAND_Gate
endmodule

module Or_Circuit (
  input  in_1,
  input  in_2,
  output out_3
);

  wire nand_1_out, nand_2_out;

  not nand_1 (nand_1_out, in_2);  // NAND_Gate
  not nand_2 (nand_2_out, in_1);  // NAND_Gate
  nand nand_3 (out_3, nand_2_out, nand_1_out);
endmodule

module Not_Circuit (
  input  in_1,
  output out_2
);

  nand nand_1 (out_2, in_1, in_1);
endmodule
