// Logisim project Lab3.6.circ as structural Verilog: 1 circuit, main circuit main
module main (
  input  in_1,
  output out_2
);

  wire and_1_out, and_2_out, and_3_out, and_4_out, decoder_1_out0, decoder_1_out1, decoder_1_out2,
       decoder_1_out3, undriven, undriven_2;

  Decoder #(.select(2)) decoder_1 (
    .out0(decoder_1_out0), .out1(decoder_1_out1), .out2(decoder_1_out2), .out3(decoder_1_out3));  // open: sel, en
  D_Flip_Flop d_ff_1 (.D(undriven), .clk(and_1_out));  // open: Q, Qn, preset, reset
  and and_1 (and_1_out, decoder_1_out0, in_1);
  D_Flip_Flop d_ff_2 (.D(undriven), .clk(and_2_out));  // open: Q, Qn, preset, reset
  and and_2 (and_2_out, decoder_1_out1, in_1);
  D_Flip_Flop d_ff_3 (.D(undriven), .clk(and_3_out));  // open: Q, Qn, preset, reset
  and and_3 (and_3_out, decoder_1_out2, in_1);
  D_Flip_Flop d_ff_4 (.D(undriven), .clk(and_4_out));  // open: Q, Qn, preset, reset
  and and_4 (and_4_out, decoder_1_out3, in_1);
  D_Flip_Flop d_ff_5 (.D(undriven_2), .clk(and_1_out), .Q(out_2));  // open: Qn, preset, reset
  D_Flip_Flop d_ff_6 (.D(undriven_2), .clk(and_2_out), .Q(out_2));  // open: Qn, preset, reset
  D_Flip_Flop d_ff_7 (.D(undriven_2), .clk(and_3_out), .Q(out_2));  // open: Qn, preset, reset
  D_Flip_Flop d_ff_8 (.D(undriven_2), .clk(and_4_out), .Q(out_2));  // open: Qn, preset, reset
endmodule
