// Logisim project lab3.2.circ as structural Verilog: 2 circuits, main circuit main
module main (
  input  in_1,
  input  in_2,
  output out_3
);

  wire nand_1_out, or_1_out;

  nand nand_1 (nand_1_out, in_1, in_2);
  or or_1 (or_1_out, in_1, in_2);
  and and_1 (out_3, nand_1_out, or_1_out);
endmodule

module Second_XOR (
  input  in_1,
  input  in_2,
  output out_3
);

  wire and_1_out, nor_1_out;

  nor nor_1 (nor_1_out, in_1, in_2);
  and and_1 (and_1_out, in_1, in_2);
  nor nor_2 (out_3, nor_1_out, and_1_out);
endmodule
